// Logisim project elapu-3.circ as structural Verilog: 2 circuits, main circuit main
module main (
);

  wire and_1_out, and_2_out, and_3_out, and_4_out, and_13_out, and_16_out, and_17_out, and_18_out,
       and_19_out, and_20_out, and_21_out, and_22_out, and_23_out, and_24_out, and_25_out, and_26_out,
       and_27_out, and_28_out, and_29_out, and_30_out, and_31_out, and_33_out, and_34_out, and_43_out,
       and_44_out, and_45_out, and_46_out, and_47_out, and_48_out, and_49_out, and_50_out, and_51_out,
       and_52_out, and_53_out, and_54_out, and_55_out, and_56_out, and_57_out, and_58_out, and_59_out,
       and_60_out, and_61_out, and_62_out, and_63_out, and_64_out, and_65_out, and_66_out, and_67_out,
       and_68_out, and_69_out, and_70_out, and_71_out, and_72_out, and_73_out, and_74_out, and_75_out,
       and_76_out, and_77_out, and_78_out, and_79_out, and_80_out, and_81_out, and_82_out, and_83_out,
       and_84_out, and_85_out, and_86_out, and_87_out, and_88_out, and_89_out, and_90_out, and_91_out,
       and_100_out, and_101_out, buffer_1_out, buffer_2_out, buffer_3_out, buffer_4_out, buffer_5_out,
       buffer_6_out, buffer_7_out, buffer_8_out, buffer_13_out, buffer_16_out, buffer_17_out, buffer_18_out,
       buffer_24_out, buffer_25_out, buffer_26_out, buffer_27_out, buffer_28_out, buffer_29_out,
       buffer_30_out, buffer_31_out, buffer_32_out, buffer_33_out, button_1_out, clock_1_out, clock_2_out,
       clock_3_out, clock_4_out, clock_5_out, clock_6_out, clock_8_out, demultiplexer_1_out2,
       demultiplexer_1_out3, demultiplexer_1_out4, demultiplexer_1_out5, demultiplexer_1_out8,
       demultiplexer_1_out15, keyboard_1_avail, nor_1_out, nor_2_out, nor_3_out, nor_4_out, nor_5_out,
       nor_6_out, nor_7_out, nor_8_out, nor_9_out, nor_10_out, nor_11_out, nor_12_out, nor_13_out,
       nor_14_out, nor_15_out, nor_16_out, nor_17_out, nor_18_out, nor_19_out, nor_20_out, nor_21_out,
       nor_22_out, nor_23_out, nor_24_out, nor_25_out, nor_34_out, not_1_out, or_1_out, or_2_out, or_3_out,
       or_4_out, or_5_out, or_6_out, or_7_out, or_8_out, or_9_out, or_10_out, or_20_out, or_21_out,
       or_22_out, or_23_out, or_24_out, or_25_out, or_26_out, or_27_out, pull_resistor_10_node,
       pull_resistor_11_node, pull_resistor_12_node, pull_resistor_13_node, pull_resistor_14_node,
       pull_resistor_15_node, pull_resistor_16_node, pull_resistor_17_node, pull_resistor_18_node,
       rgb_video_1_p2, rgb_video_1_p3, rgb_video_1_p4, rgb_video_1_p9, rgb_video_1_p14, rgb_video_1_p15,
       xor_1_out, xor_2_out, xor_3_out, xor_4_out, xor_5_out, xor_6_out, xor_7_out, xor_8_out, xor_9_out,
       xor_10_out, xor_11_out, xor_12_out, xor_13_out, xor_14_out, xor_15_out, xor_16_out, xor_17_out,
       xor_18_out, xor_19_out, xor_20_out, xor_21_out, xor_22_out, xor_23_out, xor_24_out;
  wire [3:0] and_95_out, and_99_out, rgb_video_1_p5, rgb_video_1_p5_2, rom_1_data;
  wire [7:0] and8_1_out_3, and8_2_out_3, and8_3_out_3, and8_4_out_3, and8_5_out_3, and8_6_out_3, and_5_out,
       buffer_9_out, buffer_10_out, buffer_11_out, buffer_12_out, buffer_14_out, buffer_15_out,
       buffer_19_out, buffer_20_out, buffer_21_out, buffer_22_out, buffer_23_out, keyboard_1_data, or_11_out,
       or_12_out, or_13_out, or_14_out, or_15_out, or_16_out, or_17_out, or_18_out, or_19_out,
       pull_resistor_6_node, pull_resistor_7_node, pull_resistor_8_node, ram_1_dout, register_1_q,
       register_2_q, rgb_video_1_p1, rgb_video_1_p6, rgb_video_1_p11;
  wire [11:0] counter_1_q, rom_1_data_2;
  wire [15:0] rom_2_data;

  and and_1 (and_1_out, rgb_video_1_p2, demultiplexer_1_out8);
  and and_2 (and_2_out, rom_2_data[13], nor_17_out);
  or or_1 (or_1_out, rom_2_data[3], and_2_out, and_3_out);
  and and_3 (and_3_out, rom_2_data[14], and_101_out);
  ROM #(.addrWidth(12), .dataWidth(16)) rom_1 (.addr(counter_1_q), .data({rom_1_data, rom_1_data_2}));
  Clock clock_1 (.out(clock_1_out));
  TTY #(.rows(16)) tty_1 (
    .data({rgb_video_1_p5[2:0], rgb_video_1_p5_2}), .clk(clock_1_out), .we(and_4_out), .clr(button_1_out));
  Button button_1 (.out(button_1_out));
  and and_4 (and_4_out, rgb_video_1_p3, demultiplexer_1_out4);
  // NoConnect on rom_2_data[15]
  Counter #(.max('hfff), .width(12)) counter_1 (
    .clr(button_1_out), .load(or_1_out), .clk(clock_2_out), .D(rom_1_data_2), .Q(counter_1_q));  // open: up, count, carry
  Clock clock_2 (.out(clock_2_out));
  ROM #(.addrWidth(4), .dataWidth(16)) rom_2 (.addr(rom_1_data), .data(rom_2_data));
  Keyboard keyboard_1 (
    .clk(clock_3_out), .re(and_1_out), .avail(keyboard_1_avail), .data(keyboard_1_data[6:0]));  // open: clr
  Clock clock_3 (.out(clock_3_out));
  and8 and8_1 (.in_1(register_1_q), .in_2(and_1_out), .out_3(and8_1_out_3));
  and and_5 (and_5_out[0], ~or_2_out, rom_1_data_2[0]);  // AND_Gate
  and and_6 (and_5_out[1], ~or_2_out, rom_1_data_2[1]);  // AND_Gate
  and and_7 (and_5_out[2], ~or_2_out, rom_1_data_2[2]);  // AND_Gate
  and and_8 (and_5_out[3], ~or_2_out, rom_1_data_2[3]);  // AND_Gate
  and and_9 (and_5_out[4], ~or_2_out, rom_1_data_2[4]);  // AND_Gate
  and and_10 (and_5_out[5], ~or_2_out, rom_1_data_2[5]);  // AND_Gate
  and and_11 (and_5_out[6], ~or_2_out, rom_1_data_2[6]);  // AND_Gate
  or or_2 (or_2_out, rom_1_data_2[8], rom_1_data_2[9], rom_1_data_2[10], rom_1_data_2[11]);
  and and_12 (and_5_out[7], ~or_2_out, rom_1_data_2[7]);  // AND_Gate
  // NoConnect on rom_2_data[10]
  // NoConnect on rom_2_data[9]
  // NoConnect on rom_2_data[8]
  // NoConnect on rom_2_data[7]
  // NoConnect on rom_2_data[6]
  // NoConnect on rom_2_data[4]
  // NoConnect on rom_2_data[11]
  and8 and8_2 (.in_1(rom_1_data_2[7:0]), .in_2(rom_2_data[15]), .out_3(and8_2_out_3));
  Pull_Resistor pull_resistor_1 (.node(keyboard_1_data[7]));
  Register register_1 (
    .D(keyboard_1_data), .en(keyboard_1_avail), .clk(clock_4_out), .Q(register_1_q), .clr(clock_5_out));
  Clock clock_4 (.out(clock_4_out));
  Clock #(.phaseOffset(1)) clock_5 (.out(clock_5_out));
  Pull_Resistor pull_resistor_2 (.node(rgb_video_1_p5[3]));
  buf buffer_1 (buffer_1_out, or_2_out);
  buf buffer_2 (buffer_2_out, buffer_1_out);
  buf buffer_3 (buffer_3_out, buffer_2_out);
  buf buffer_4 (buffer_4_out, buffer_3_out);
  buf buffer_5 (buffer_5_out, buffer_4_out);
  buf buffer_6 (buffer_6_out, buffer_5_out);
  buf buffer_7 (buffer_7_out, buffer_6_out);
  buf buffer_8 (buffer_8_out, buffer_7_out);
  // NoConnect on rom_2_data[2]
  assign buffer_9_out = and8_2_out_3;  // Buffer buffer_9, 8 bits wide
  assign buffer_10_out = buffer_9_out;  // Buffer buffer_10, 8 bits wide
  assign buffer_11_out = buffer_10_out;  // Buffer buffer_11, 8 bits wide
  assign buffer_12_out = buffer_11_out;  // Buffer buffer_12, 8 bits wide
  and and_13 (and_13_out, rgb_video_1_p9, rgb_video_1_p2);
  Register register_2 (
    .D({rgb_video_1_p5, rgb_video_1_p5_2}), .en(rom_2_data[5]), .clk(clock_6_out), .Q(register_2_q));  // open: clr
  Clock clock_6 (.out(clock_6_out));
  buf buffer_13 (buffer_13_out, rom_2_data[12]);
  and8 and8_3 (.in_1(and_5_out), .in_2(not_1_out), .out_3(and8_3_out_3));
  not not_1 (not_1_out, rom_2_data[12]);
  // NoConnect on rom_2_data[1]
  or or_3 (or_3_out, buffer_19_out[3], buffer_15_out[3], and_99_out[3]);
  or or_4 (or_4_out, buffer_19_out[4], buffer_15_out[4], and_95_out[0]);
  or or_5 (or_5_out, buffer_19_out[5], buffer_15_out[5], and_95_out[1]);
  or or_6 (or_6_out, buffer_19_out[6], buffer_15_out[6], and_95_out[2]);
  or or_7 (or_7_out, buffer_19_out[7], buffer_15_out[7], and_95_out[3]);
  assign buffer_14_out = buffer_12_out;  // Buffer buffer_14, 8 bits wide
  assign buffer_15_out = buffer_14_out;  // Buffer buffer_15, 8 bits wide
  // RGB_Video #(.cursor("No Cursor"), .height(16), .scale(8), .width(16)) rgb_video_1: pin names not known; wires that end beside it: rgb_video_1_p1, rgb_video_1_p2, rgb_video_1_p3, rgb_video_1_p4, {rgb_video_1_p5, rgb_video_1_p5_2}, rgb_video_1_p6, rgb_video_1_p2, rgb_video_1_p3, rgb_video_1_p9, {rgb_video_1_p5, rgb_video_1_p5_2}, rgb_video_1_p11, rgb_video_1_p2, and_13_out, rgb_video_1_p14, rgb_video_1_p15, rgb_video_1_p5, rgb_video_1_p5_2, 4'b1111, rgb_video_1_p3, rgb_video_1_p2, {rgb_video_1_p5, rgb_video_1_p5_2}
  Clock clock_7 (.out(rgb_video_1_p14));
  and and_14 (rgb_video_1_p15, rgb_video_1_p9, rgb_video_1_p3);
  Demultiplexer #(.select(4)) demultiplexer_1 (
    .out2(demultiplexer_1_out2), .out3(demultiplexer_1_out3), .out4(demultiplexer_1_out4),
    .out5(demultiplexer_1_out5), .out6(rgb_video_1_p9), .out7(rgb_video_1_p4), .out8(demultiplexer_1_out8),
    .out15(demultiplexer_1_out15), .in(1'b1),
    .sel({rom_1_data_2[8], rom_1_data_2[9], rom_1_data_2[10], rom_1_data_2[11]}));  // open: out0, out1, out9, out10, out11, out12, out13, out14
  or or_8 (or_8_out, buffer_19_out[0], buffer_15_out[0], and_99_out[0]);
  or or_9 (or_9_out, buffer_19_out[1], buffer_15_out[1], and_99_out[1]);
  or or_10 (or_10_out, buffer_19_out[2], buffer_15_out[2], and_99_out[2]);
  and and_15 (rgb_video_1_p3, rom_2_data[1], or_2_out);
  and8 and8_4 (.in_1(register_2_q), .in_2(buffer_13_out), .out_3(and8_4_out_3));
  buf buffer_16 (buffer_16_out, buffer_8_out);
  buf buffer_17 (buffer_17_out, buffer_16_out);
  buf buffer_18 (buffer_18_out, buffer_17_out);
  and and_16 (and_16_out, ~or_7_out, rom_2_data[2]);  // AND_Gate
  nor nor_1 (nor_1_out, nor_9_out, and_17_out);
  and and_17 (and_17_out, rom_2_data[2], or_7_out);
  and and_18 (and_18_out, ~or_6_out, rom_2_data[2]);  // AND_Gate
  nor nor_2 (nor_2_out, nor_10_out, and_19_out);
  and and_19 (and_19_out, rom_2_data[2], or_6_out);
  and and_20 (and_20_out, ~or_5_out, rom_2_data[2]);  // AND_Gate
  nor nor_3 (nor_3_out, nor_11_out, and_21_out);
  and and_21 (and_21_out, rom_2_data[2], or_5_out);
  and and_22 (and_22_out, ~or_4_out, rom_2_data[2]);  // AND_Gate
  nor nor_4 (nor_4_out, nor_12_out, and_23_out);
  and and_23 (and_23_out, rom_2_data[2], or_4_out);
  and and_24 (and_24_out, ~or_3_out, rom_2_data[2]);  // AND_Gate
  nor nor_5 (nor_5_out, nor_13_out, and_25_out);
  and and_25 (and_25_out, rom_2_data[2], or_3_out);
  and and_26 (and_26_out, ~or_10_out, rom_2_data[2]);  // AND_Gate
  nor nor_6 (nor_6_out, nor_14_out, and_27_out);
  and and_27 (and_27_out, rom_2_data[2], or_10_out);
  and and_28 (and_28_out, ~or_9_out, rom_2_data[2]);  // AND_Gate
  nor nor_7 (nor_7_out, nor_15_out, and_29_out);
  and and_29 (and_29_out, rom_2_data[2], or_9_out);
  and and_30 (and_30_out, ~or_8_out, rom_2_data[2]);  // AND_Gate
  nor nor_8 (nor_8_out, nor_16_out, and_31_out);
  and and_31 (and_31_out, rom_2_data[2], or_8_out);
  assign buffer_19_out = buffer_20_out;  // Buffer buffer_19, 8 bits wide
  assign buffer_20_out = buffer_21_out;  // Buffer buffer_20, 8 bits wide
  assign buffer_21_out = buffer_22_out;  // Buffer buffer_21, 8 bits wide
  assign buffer_22_out = buffer_23_out;  // Buffer buffer_22, 8 bits wide
  Pull_Resistor pull_resistor_3 (.node(rgb_video_1_p1));
  Pull_Resistor pull_resistor_4 (.node(rgb_video_1_p6));
  assign or_11_out = rgb_video_1_p1 | {8{1'b0}};  // OR_Gate or_11, 8 bits wide
  Pull_Resistor pull_resistor_5 (.node(rgb_video_1_p11));
  assign or_12_out = rgb_video_1_p6 | or_11_out;  // OR_Gate or_12, 8 bits wide
  Pull_Resistor pull_resistor_6 (.node(pull_resistor_6_node));
  assign or_13_out = rgb_video_1_p11 | or_12_out;  // OR_Gate or_13, 8 bits wide
  Pull_Resistor pull_resistor_7 (.node(pull_resistor_7_node));
  assign or_14_out = pull_resistor_6_node | or_13_out;  // OR_Gate or_14, 8 bits wide
  Pull_Resistor pull_resistor_8 (.node(pull_resistor_8_node));
  assign or_15_out = pull_resistor_7_node | or_14_out;  // OR_Gate or_15, 8 bits wide
  Pull_Resistor pull_resistor_9 (.node(and8_1_out_3));
  assign or_16_out = pull_resistor_8_node | or_15_out;  // OR_Gate or_16, 8 bits wide
  and and_32 (rgb_video_1_p2, rom_2_data[0], or_2_out);
  assign or_17_out = and8_1_out_3 | or_16_out;  // OR_Gate or_17, 8 bits wide
  and and_33 (and_33_out, rom_2_data[1], ~buffer_18_out);  // AND_Gate
  and and_34 (and_34_out, rom_2_data[0], ~buffer_18_out);  // AND_Gate
  nor nor_9 (nor_9_out, and_16_out, nor_1_out);
  and and_35 (rgb_video_1_p5[3], nor_9_out, rom_2_data[4]);
  nor nor_10 (nor_10_out, and_18_out, nor_2_out);
  and and_36 (rgb_video_1_p5[2], nor_10_out, rom_2_data[4]);
  nor nor_11 (nor_11_out, and_20_out, nor_3_out);
  and and_37 (rgb_video_1_p5[1], nor_11_out, rom_2_data[4]);
  nor nor_12 (nor_12_out, and_22_out, nor_4_out);
  and and_38 (rgb_video_1_p5[0], nor_12_out, rom_2_data[4]);
  nor nor_13 (nor_13_out, and_24_out, nor_5_out);
  and and_39 (rgb_video_1_p5_2[3], nor_13_out, rom_2_data[4]);
  nor nor_14 (nor_14_out, and_26_out, nor_6_out);
  and and_40 (rgb_video_1_p5_2[2], nor_14_out, rom_2_data[4]);
  nor nor_15 (nor_15_out, and_28_out, nor_7_out);
  and and_41 (rgb_video_1_p5_2[1], nor_15_out, rom_2_data[4]);
  nor nor_16 (nor_16_out, and_30_out, nor_8_out);
  and and_42 (rgb_video_1_p5_2[0], nor_16_out, rom_2_data[4]);
  assign buffer_23_out = or_19_out;  // Buffer buffer_23, 8 bits wide
  RAM #(.asyncread("true"), .trigger("falling")) ram_1 (
    .addr(or_18_out), .we(and_33_out), .oe(and_34_out), .clk(clock_8_out),
    .din({rgb_video_1_p5, rgb_video_1_p5_2}), .dout(ram_1_dout));
  Clock clock_8 (.out(clock_8_out));
  assign or_18_out = and8_4_out_3 | and8_3_out_3;  // OR_Gate or_18, 8 bits wide
  and and_43 (and_43_out, rgb_video_1_p5[3], rom_2_data[0]);
  and and_44 (and_44_out, rgb_video_1_p5[2], rom_2_data[0]);
  and and_45 (and_45_out, rgb_video_1_p5[1], rom_2_data[0]);
  and and_46 (and_46_out, rgb_video_1_p5[0], rom_2_data[0]);
  and and_47 (and_47_out, rgb_video_1_p5_2[3], rom_2_data[0]);
  and and_48 (and_48_out, rgb_video_1_p5_2[2], rom_2_data[0]);
  and and_49 (and_49_out, rgb_video_1_p5_2[1], rom_2_data[0]);
  and and_50 (and_50_out, rgb_video_1_p5_2[0], rom_2_data[0]);
  and8 and8_5 (.in_1(or_17_out), .in_2(rgb_video_1_p2), .out_3(and8_5_out_3));
  and and_51 (and_51_out, or_19_out[0], rom_2_data[11]);
  xor xor_1 (xor_1_out, rom_2_data[6], and_43_out);
  xor xor_2 (xor_2_out, rom_2_data[6], and_44_out);
  xor xor_3 (xor_3_out, rom_2_data[6], and_45_out);
  xor xor_4 (xor_4_out, rom_2_data[6], and_46_out);
  xor xor_5 (xor_5_out, rom_2_data[6], and_47_out);
  xor xor_6 (xor_6_out, rom_2_data[6], and_48_out);
  xor xor_7 (xor_7_out, rom_2_data[6], and_49_out);
  xor xor_8 (xor_8_out, rom_2_data[6], and_50_out);
  buf buffer_24 (buffer_24_out, rom_2_data[7]);
  buf buffer_25 (buffer_25_out, buffer_24_out);
  buf buffer_26 (buffer_26_out, buffer_25_out);
  buf buffer_27 (buffer_27_out, buffer_26_out);
  and and_52 (and_52_out, or_19_out[1], rom_2_data[11]);
  xor xor_9 (xor_9_out, and_90_out, xor_1_out);
  xor xor_10 (xor_10_out, and_89_out, xor_2_out);
  xor xor_11 (xor_11_out, and_72_out, xor_3_out);
  xor xor_12 (xor_12_out, and_71_out, xor_4_out);
  xor xor_13 (xor_13_out, and_54_out, xor_5_out);
  xor xor_14 (xor_14_out, and_53_out, xor_6_out);
  xor xor_15 (xor_15_out, and_52_out, xor_7_out);
  xor xor_16 (xor_16_out, and_51_out, xor_8_out);
  buf buffer_28 (buffer_28_out, buffer_27_out);
  buf buffer_29 (buffer_29_out, buffer_28_out);
  buf buffer_30 (buffer_30_out, buffer_29_out);
  buf buffer_31 (buffer_31_out, buffer_30_out);
  and8 and8_6 (.in_1(ram_1_dout), .in_2(and_34_out), .out_3(and8_6_out_3));
  and and_53 (and_53_out, or_19_out[2], rom_2_data[11]);
  and and_54 (and_54_out, or_19_out[3], rom_2_data[11]);
  xor xor_17 (xor_17_out, xor_9_out, or_21_out);
  and and_55 (and_55_out, or_21_out, xor_9_out);
  and and_56 (and_56_out, xor_1_out, and_90_out);
  xor xor_18 (xor_18_out, xor_10_out, or_22_out);
  and and_57 (and_57_out, or_22_out, xor_10_out);
  and and_58 (and_58_out, xor_2_out, and_89_out);
  xor xor_19 (xor_19_out, xor_11_out, or_23_out);
  and and_59 (and_59_out, or_23_out, xor_11_out);
  and and_60 (and_60_out, xor_3_out, and_72_out);
  xor xor_20 (xor_20_out, xor_12_out, or_24_out);
  and and_61 (and_61_out, or_24_out, xor_12_out);
  and and_62 (and_62_out, xor_4_out, and_71_out);
  xor xor_21 (xor_21_out, xor_13_out, or_25_out);
  and and_63 (and_63_out, or_25_out, xor_13_out);
  and and_64 (and_64_out, xor_5_out, and_54_out);
  xor xor_22 (xor_22_out, xor_14_out, or_26_out);
  and and_65 (and_65_out, or_26_out, xor_14_out);
  and and_66 (and_66_out, xor_6_out, and_53_out);
  xor xor_23 (xor_23_out, xor_15_out, or_27_out);
  and and_67 (and_67_out, or_27_out, xor_15_out);
  and and_68 (and_68_out, xor_7_out, and_52_out);
  xor xor_24 (xor_24_out, xor_16_out, buffer_33_out);
  and and_69 (and_69_out, buffer_33_out, xor_16_out);
  and and_70 (and_70_out, xor_8_out, and_51_out);
  buf buffer_32 (buffer_32_out, buffer_31_out);
  buf buffer_33 (buffer_33_out, buffer_32_out);
  assign or_19_out = and8_6_out_3 | and8_5_out_3;  // OR_Gate or_19, 8 bits wide
  and and_71 (and_71_out, or_19_out[4], rom_2_data[11]);
  or or_20 (or_20_out, and_55_out, and_56_out);
  or or_21 (or_21_out, and_57_out, and_58_out);
  or or_22 (or_22_out, and_59_out, and_60_out);
  or or_23 (or_23_out, and_61_out, and_62_out);
  or or_24 (or_24_out, and_63_out, and_64_out);
  or or_25 (or_25_out, and_65_out, and_66_out);
  or or_26 (or_26_out, and_67_out, and_68_out);
  or or_27 (or_27_out, and_69_out, and_70_out);
  nor nor_17 (nor_17_out, and_99_out[0], and_99_out[1], and_99_out[2], and_99_out[3], and_95_out[0], and_95_out[1], and_95_out[2], and_95_out[3]);
  and and_72 (and_72_out, or_19_out[5], rom_2_data[11]);
  and and_73 (and_73_out, ~xor_17_out, rom_2_data[8]);  // AND_Gate
  nor nor_18 (nor_18_out, pull_resistor_10_node, and_74_out);
  and and_74 (and_74_out, rom_2_data[8], xor_17_out);
  and and_75 (and_75_out, ~xor_18_out, rom_2_data[8]);  // AND_Gate
  nor nor_19 (nor_19_out, pull_resistor_11_node, and_76_out);
  and and_76 (and_76_out, rom_2_data[8], xor_18_out);
  and and_77 (and_77_out, ~xor_19_out, rom_2_data[8]);  // AND_Gate
  nor nor_20 (nor_20_out, pull_resistor_12_node, and_78_out);
  and and_78 (and_78_out, rom_2_data[8], xor_19_out);
  and and_79 (and_79_out, ~xor_20_out, rom_2_data[8]);  // AND_Gate
  nor nor_21 (nor_21_out, pull_resistor_13_node, and_80_out);
  and and_80 (and_80_out, rom_2_data[8], xor_20_out);
  and and_81 (and_81_out, ~xor_21_out, rom_2_data[8]);  // AND_Gate
  nor nor_22 (nor_22_out, pull_resistor_14_node, and_82_out);
  and and_82 (and_82_out, rom_2_data[8], xor_21_out);
  and and_83 (and_83_out, ~xor_22_out, rom_2_data[8]);  // AND_Gate
  nor nor_23 (nor_23_out, pull_resistor_15_node, and_84_out);
  and and_84 (and_84_out, rom_2_data[8], xor_22_out);
  and and_85 (and_85_out, ~xor_23_out, rom_2_data[8]);  // AND_Gate
  nor nor_24 (nor_24_out, pull_resistor_16_node, and_86_out);
  and and_86 (and_86_out, rom_2_data[8], xor_23_out);
  and and_87 (and_87_out, ~xor_24_out, rom_2_data[8]);  // AND_Gate
  nor nor_25 (nor_25_out, pull_resistor_17_node, and_88_out);
  and and_88 (and_88_out, rom_2_data[8], xor_24_out);
  and and_89 (and_89_out, or_19_out[6], rom_2_data[11]);
  and and_90 (and_90_out, or_19_out[7], rom_2_data[11]);
  Pull_Resistor pull_resistor_10 (.node(pull_resistor_10_node));
  nor nor_26 (pull_resistor_10_node, and_73_out, nor_18_out);
  Pull_Resistor pull_resistor_11 (.node(pull_resistor_11_node));
  nor nor_27 (pull_resistor_11_node, and_75_out, nor_19_out);
  Pull_Resistor pull_resistor_12 (.node(pull_resistor_12_node));
  nor nor_28 (pull_resistor_12_node, and_77_out, nor_20_out);
  Pull_Resistor pull_resistor_13 (.node(pull_resistor_13_node));
  nor nor_29 (pull_resistor_13_node, and_79_out, nor_21_out);
  Pull_Resistor pull_resistor_14 (.node(pull_resistor_14_node));
  nor nor_30 (pull_resistor_14_node, and_81_out, nor_22_out);
  Pull_Resistor pull_resistor_15 (.node(pull_resistor_15_node));
  nor nor_31 (pull_resistor_15_node, and_83_out, nor_23_out);
  Pull_Resistor pull_resistor_16 (.node(pull_resistor_16_node));
  nor nor_32 (pull_resistor_16_node, and_85_out, nor_24_out);
  Pull_Resistor pull_resistor_17 (.node(pull_resistor_17_node));
  nor nor_33 (pull_resistor_17_node, and_87_out, nor_25_out);
  and and_91 (and_91_out, ~or_20_out, rom_2_data[8]);  // AND_Gate
  nor nor_34 (nor_34_out, pull_resistor_18_node, and_100_out);
  and and_92 (and_95_out[3], pull_resistor_10_node, rom_2_data[10]);
  and and_93 (and_95_out[2], pull_resistor_11_node, rom_2_data[10]);
  and and_94 (and_95_out[1], pull_resistor_12_node, rom_2_data[10]);
  and and_95 (and_95_out[0], pull_resistor_13_node, rom_2_data[10]);
  and and_96 (and_99_out[3], pull_resistor_14_node, rom_2_data[10]);
  and and_97 (and_99_out[2], pull_resistor_15_node, rom_2_data[10]);
  and and_98 (and_99_out[1], pull_resistor_16_node, rom_2_data[10]);
  and and_99 (and_99_out[0], pull_resistor_17_node, rom_2_data[10]);
  Pull_Resistor pull_resistor_18 (.node(pull_resistor_18_node));
  nor nor_35 (pull_resistor_18_node, and_91_out, nor_34_out);
  and and_100 (and_100_out, rom_2_data[8], or_20_out);
  and and_101 (and_101_out, pull_resistor_18_node, rom_2_data[10]);

  // Notes on the sheet:
  //   0: NOP
  //   1: LOAD
  //   2: STORE
  //   3: ADD
  //   4: SUB
  //   5: COMMIT
  //   6: IMM
  //   7: JMP
  //   8: JZ
  //   9: JC
  //   A: RDA
  //   B: WDA
  //   C: SDA
  //   contents of rom_1 (hex, n*v repeats v):
  //   600a 2000 1600 6000 2001 6010 20fe 1001 20ff 10ff 40fe 5000 803a 900f 703a 6005 2002 3002 5000 2002
  //   3002 5000 2002 3002 5000 2002 3002 5000 2002 1001 3002 5000 2600 600a 2002 3002 5000 2002 3002 5000
  //   2002 3002 5000 2002 3002 5000 2002 1001 3002 5000 2600 6001 20ff 1001 30ff 5000 2001 7005 6000 2003
  //   6010 20fe 1003 20ff 10ff 40fe 5000 8071 9046 7071 1003 2002 3002 5000 2002 3002 5000 2002 3002 5000
  //   2002 3002 5000 2002 6005 3002 5000 2600 1003 2002 3002 5000 2002 3002 5000 2002 3002 5000 2002 3002
  //   5000 2002 600a 3002 5000 2600 6001 20ff 1003 30ff 5000 2003 703c 6002 20fc 6000 20fd 6004 30fd 5000
  //   c000 10fc b000 6002 20fc 6000 20fd 600d 30fd 5000 c000 10fc b000 6007 20fc 6001 20fd 6004 30fd 5000
  //   c000 10fc b000 6002 20fc 6001 20fd 600d 30fd 5000 c000 10fc b000 600c 20fc 6002 20fd 6004 30fd 5000
  //   c000 10fc b000 6002 20fc 6002 20fd 600d 30fd 5000 c000 10fc b000 6002 20fc 6003 20fd 6004 30fd 5000
  //   c000 10fc b000 6007 20fc 6003 20fd 600d 30fd 5000 c000 10fc b000 6007 20fc 6004 20fd 6004 30fd 5000
  //   c000 10fc b000 6007 20fc 6004 20fd 600d 30fd 5000 c000 10fc b000 600c 20fc 6005 20fd 6004 30fd 5000
  //   c000 10fc b000 6007 20fc 6005 20fd 600d 30fd 5000 c000 10fc b000 6002 20fc 6006 20fd 6004 30fd 5000
  //   c000 10fc b000 600c 20fc 6006 20fd 600d 30fd 5000 c000 10fc b000 6007 20fc 6007 20fd 6004 30fd 5000
  //   c000 10fc b000 600c 20fc 6007 20fd 600d 30fd 5000 c000 10fc b000 600c 20fc 6008 20fd 6004 30fd 5000
  //   c000 10fc b000 600c 20fc 6008 20fd 600d 30fd 5000 c000 10fc b000 6000 20fc 6000 20fd 6016 30fd 5000
  //   c000 10fc b000 6000 20fc 6001 20fd 6016 30fd 5000 c000 10fc b000 6000 20fc 6002 20fd 6016 30fd 5000
  //   c000 10fc b000 6000 20fc 6003 20fd 6016 30fd 5000 c000 10fc b000 6000 20fc 6004 20fd 6016 30fd 5000
  //   c000 10fc b000 6000 20fc 6005 20fd 6016 30fd 5000 c000 10fc b000 6000 20fc 6006 20fd 6016 30fd 5000
  //   c000 10fc b000 6000 20fc 6007 20fd 6016 30fd 5000 c000 10fc b000 6000 20fc 6008 20fd 6016 30fd 5000
  //   c000 10fc b000 6000 20fc 6000 20fd 601f 30fd 5000 c000 10fc b000 6001 20fc 6001 20fd 601f 30fd 5000
  //   c000 10fc b000 6002 20fc 6002 20fd 601f 30fd 5000 c000 10fc b000 6003 20fc 6003 20fd 601f 30fd 5000
  //   c000 10fc b000 6004 20fc 6004 20fd 601f 30fd 5000 c000 10fc b000 6005 20fc 6005 20fd 601f 30fd 5000
  //   c000 10fc b000 6006 20fc 6006 20fd 601f 30fd 5000 c000 10fc b000 6007 20fc 6007 20fd 601f 30fd 5000
  //   c000 10fc b000 6008 20fc 6008 20fd 601f 30fd 5000 c000 10fc b000 6000 20fc 6009 20fd 601f 30fd 5000
  //   c000 10fc b000 6003 20fc 600a 20fd 601f 30fd 5000 c000 10fc b000 6006 20fc 600b 20fd 601f 30fd 5000
  //   c000 10fc b000 6001 20fc 600c 20fd 601f 30fd 5000 c000 10fc b000 6004 20fc 600d 20fd 601f 30fd 5000
  //   c000 10fc b000 6007 20fc 600e 20fd 601f 30fd 5000 c000 10fc b000 6002 20fc 600f 20fd 601f 30fd 5000
  //   c000 10fc b000 6005 20fc 6010 20fd 601f 30fd 5000 c000 10fc b000 6008 20fc 6011 20fd 601f 30fd 5000
  //   c000 10fc b000 6000 20fc 6012 20fd 601f 30fd 5000 c000 10fc b000 6004 20fc 6013 20fd 601f 30fd 5000
  //   c000 10fc b000 6008 20fc 6014 20fd 601f 30fd 5000 c000 10fc b000 6002 20fc 6015 20fd 601f 30fd 5000
  //   c000 10fc b000 6004 20fc 6016 20fd 601f 30fd 5000 c000 10fc b000 6006 20fc 6017 20fd 601f 30fd 5000
  //   c000 10fc b000 6000 2037 6000 2038 6000 2039 603d 2200 603d 2200 603d 2200 603d 2200 603d 2200 603d
  //   2200 603d 2200 603d 2200 603d 2200 603d 2200 603d 2200 603d 2200 603d 2200 603d 2200 603d 2200 603d
  //   2200 603d 2200 603d 2200 603d 2200 603d 2200 603d 2200 603d 2200 603d 2200 603d 2200 1000 2200 6020
  //   2200 6020 2200 6045 2200 604c 2200 6041 2200 6050 2200 6055 2200 602d 2200 6033 2200 6020 2200 6054
  //   2200 6049 2200 6043 2200 602d 2200 6054 2200 6041 2200 6043 2200 602d 2200 6054 2200 604f 2200 6045
  //   2200 6020 2200 6020 2200 6020 2200 1000 2200 603d 2200 603d 2200 603d 2200 603d 2200 603d 2200 603d
  //   2200 603d 2200 603d 2200 603d 2200 603d 2200 603d 2200 603d 2200 603d 2200 603d 2200 603d 2200 603d
  //   2200 603d 2200 603d 2200 603d 2200 603d 2200 603d 2200 603d 2200 603d 2200 603d 2200 1000 2200 6048
  //   2200 6075 2200 606d 2200 6061 2200 606e 2200 603a 2200 6020 2200 6058 2200 6020 2200 6020 2200 607c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
  //   contents of rom_2 (hex, n*v repeats v):
  //   0 5 12 911 9d1 404 8004 8 2400 4400 1005 1012 30
  //   out,read,write,select
endmodule

module and8 (
  input  [7:0] in_1,
  input  in_2,
  output [7:0] out_3
);

  and and_1 (out_3[0], in_1[0], in_2);
  and and_2 (out_3[1], in_1[1], in_2);
  and and_3 (out_3[2], in_1[2], in_2);
  and and_4 (out_3[3], in_1[3], in_2);
  and and_5 (out_3[4], in_1[4], in_2);
  and and_6 (out_3[5], in_1[5], in_2);
  and and_7 (out_3[6], in_1[6], in_2);
  and and_8 (out_3[7], in_1[7], in_2);
endmodule
